// Logisim project banco_de_registradores.circ as structural Verilog: 1 circuit, main circuit main
module main (
);

  Register #(.width(4)) register_1 ();  // open: D, en, Q, clk, clr
  Register #(.width(4)) register_2 ();  // open: D, en, Q, clk, clr
  Register #(.width(4)) register_3 ();  // open: D, en, Q, clk, clr
  Register #(.width(4)) register_4 ();  // open: D, en, Q, clk, clr
  Register #(.width(4)) register_5 ();  // open: D, en, Q, clk, clr
  Register #(.width(4)) register_6 ();  // open: D, en, Q, clk, clr
  Register #(.width(4)) register_7 ();  // open: D, en, Q, clk, clr
  Register #(.width(4)) register_8 ();  // open: D, en, Q, clk, clr
  Register #(.width(4)) register_9 ();  // open: D, en, Q, clk, clr
  Register #(.width(4)) register_10 ();  // open: D, en, Q, clk, clr
endmodule
