// Logisim project processador.circ as structural Verilog: 23 circuits, main circuit main
module main (
  input  N3,
  input  N2,
  input  N1,
  input  N0,
  input  LOAD_IN
);

  wire clock_1_out, CY_carry_in, memoria_de_dados_1_p3, memoria_de_dados_1_p4, ULA_c_out, undriven_2,
       undriven_7, undriven_8, undriven_10, undriven_11, undriven_12, undriven_13, undriven_14;
  wire [3:0] ACC_acc_out, adder_2_out, banco_de_registradores_ula_a, banco_de_registradores_ula_b,
       entrada_n_1_n, memoria_de_dados_1_p6, multiplexer_1_out, multiplexer_2_out, multiplexer_3_out,
       multiplexer_4_out, multiplexer_5_out, multiplexer_6_out, PC_4, PC_pc, ULA, undriven, undriven_3,
       undriven_4, undriven_5, undriven_6, undriven_9;

  Adder #(.width(4)) adder_1 (.a(PC_pc), .b(4'b0100), .out(PC_4));  // open: cin, cout
  Adder #(.width(4)) adder_2 (.a(PC_pc), .b(undriven), .out(adder_2_out));  // open: cin, cout
  Multiplexer #(.select(2), .width(4)) multiplexer_1 (
    .in1(PC_4), .in2(adder_2_out), .in3(ULA), .out(multiplexer_1_out));  // open: in0, sel, en
  Clock clock_1 (.out(clock_1_out));
  PC PC (.PC_In(multiplexer_1_out), .Seletor_PC(undriven_2), .clk(clock_1_out), .PC(PC_pc));
  banco_de_registradores banco_de_registradores (
    .RD(undriven_4), .Resultado(multiplexer_6_out), .clk(clock_1_out), .WriteEn(undriven_7),
    .RG1(undriven_5), .RG2(undriven_6), .ULA_A(banco_de_registradores_ula_a),
    .ULA_B(banco_de_registradores_ula_b));
  ACC ACC (.ACC_In(ULA), .clk(clock_1_out), .ACC_Out(ACC_acc_out));  // open: ACC_Load
  CY CY (.Carry_ULA(ULA_c_out), .clk(clock_1_out), .Carry_Write(undriven_8), .Carry_In(CY_carry_in));
  Multiplexer #(.width(4)) multiplexer_2 (
    .in0(banco_de_registradores_ula_a), .in1(ACC_acc_out), .out(multiplexer_2_out));  // open: sel, en
  Multiplexer #(.select(2), .width(4)) multiplexer_3 (
    .in1(banco_de_registradores_ula_b), .in2(undriven_9), .in3(ACC_acc_out), .out(multiplexer_3_out));  // open: in0, sel, en
  ULA u_ULA (
    .A(multiplexer_2_out), .B(multiplexer_3_out), .C_In(CY_carry_in), .S2(undriven_10), .S1(undriven_11),
    .S0(undriven_12), .SAIDA(ULA), .C_out(ULA_c_out));  // open: OVERFLOW
  Multiplexer #(.width(4)) multiplexer_4 (
    .in0(ULA), .in1(banco_de_registradores_ula_a), .out(multiplexer_4_out), .en(undriven_13));  // open: sel
  Multiplexer #(.width(4)) multiplexer_5 (
    .in0(undriven_3), .in1(banco_de_registradores_ula_b), .out(multiplexer_5_out), .en(undriven_14));  // open: sel
  // memoria_de_dados memoria_de_dados_1: pin names not known; wires that end beside it: multiplexer_5_out, multiplexer_4_out, memoria_de_dados_1_p3, memoria_de_dados_1_p4, clock_1_out, memoria_de_dados_1_p6
  Entrada_N entrada_n_1 (.clk(clock_1_out), .N3(N3), .N2(N2), .N1(N1), .N0(N0), .LOAD_IN(LOAD_IN), .N(entrada_n_1_n));
  Multiplexer #(.select(2), .width(4)) multiplexer_6 (
    .in0(ULA), .in1(memoria_de_dados_1_p6), .in2(entrada_n_1_n), .in3(PC_4), .out(multiplexer_6_out));  // open: sel, en

  // Notes on the sheet:
  //   PC_SELECT
  //   Instrução
  //   Instrução
  //   Imediato
  //   Shifter e extensor??
  //   Centro de controle
endmodule

module banco_de_registradores (
  input  [3:0] RD,
  input  [3:0] Resultado,
  input  clk,
  input  WriteEn,
  input  [3:0] RG1,
  input  [3:0] RG2,
  output [3:0] ULA_A,
  output [3:0] ULA_B
);

  wire decoder_1_out0, decoder_1_out1, decoder_1_out2, decoder_1_out3, decoder_1_out4, decoder_1_out5,
       decoder_1_out6, decoder_1_out7, decoder_1_out8, decoder_1_out9, decoder_1_out10, decoder_1_out11,
       decoder_1_out12, decoder_1_out13, decoder_1_out14, decoder_1_out15;
  wire [3:0] registradores_1_r0, registradores_1_r1, registradores_1_r2, registradores_1_r3,
       registradores_1_r4, registradores_1_r5, registradores_1_r6, registradores_1_r7, registradores_1_r8,
       registradores_1_r9, registradores_1_r10, registradores_1_r11, registradores_1_r12,
       registradores_1_r13, registradores_1_ra_2, registradores_1_sp_2;

  Decoder #(.select(4)) decoder_1 (
    .out0(decoder_1_out0), .out1(decoder_1_out1), .out2(decoder_1_out2), .out3(decoder_1_out3),
    .out4(decoder_1_out4), .out5(decoder_1_out5), .out6(decoder_1_out6), .out7(decoder_1_out7),
    .out8(decoder_1_out8), .out9(decoder_1_out9), .out10(decoder_1_out10), .out11(decoder_1_out11),
    .out12(decoder_1_out12), .out13(decoder_1_out13), .out14(decoder_1_out14), .out15(decoder_1_out15),
    .sel(RD));  // open: en
  registradores registradores_1 (
    .Load(Resultado), .en0(decoder_1_out0), .en1(decoder_1_out1), .en2(decoder_1_out2), .en3(decoder_1_out3),
    .en4(decoder_1_out4), .en5(decoder_1_out5), .en6(decoder_1_out6), .en7(decoder_1_out7),
    .en8(decoder_1_out8), .en9(decoder_1_out9), .en10(decoder_1_out10), .en11(decoder_1_out11),
    .en12(decoder_1_out12), .en13(decoder_1_out13), .SP(decoder_1_out14), .RA(decoder_1_out15),
    .WriteEnable(WriteEn), .clk(clk), .R0(registradores_1_r0), .R1(registradores_1_r1),
    .R2(registradores_1_r2), .R3(registradores_1_r3), .R4(registradores_1_r4), .R5(registradores_1_r5),
    .R6(registradores_1_r6), .R7(registradores_1_r7), .R8(registradores_1_r8), .R9(registradores_1_r9),
    .R10(registradores_1_r10), .R11(registradores_1_r11), .R12(registradores_1_r12),
    .R13(registradores_1_r13), .SP_2(registradores_1_sp_2), .RA_2(registradores_1_ra_2));
  Multiplexer #(.select(4), .width(4)) multiplexer_1 (
    .in0(registradores_1_r0), .in1(registradores_1_r1), .in2(registradores_1_r2), .in3(registradores_1_r3),
    .in4(registradores_1_r4), .in5(registradores_1_r5), .in6(registradores_1_r6), .in7(registradores_1_r7),
    .in8(registradores_1_r8), .in9(registradores_1_r9), .in10(registradores_1_r10),
    .in11(registradores_1_r11), .in12(registradores_1_r12), .in13(registradores_1_r13),
    .in14(registradores_1_sp_2), .in15(registradores_1_ra_2), .out(ULA_A), .sel(RG1));  // open: en
  Multiplexer #(.select(4), .width(4)) multiplexer_2 (
    .in0(registradores_1_r0), .in1(registradores_1_r1), .in2(registradores_1_r2), .in3(registradores_1_r3),
    .in4(registradores_1_r4), .in5(registradores_1_r5), .in6(registradores_1_r6), .in7(registradores_1_r7),
    .in8(registradores_1_r8), .in9(registradores_1_r9), .in10(registradores_1_r10),
    .in11(registradores_1_r11), .in12(registradores_1_r12), .in13(registradores_1_r13),
    .in14(registradores_1_sp_2), .in15(registradores_1_ra_2), .out(ULA_B), .sel(RG2));  // open: en
endmodule

module registradores (
  input  [3:0] Load,
  input  en0,
  input  en1,
  input  en2,
  input  en3,
  input  en4,
  input  en5,
  input  en6,
  input  en7,
  input  en8,
  input  en9,
  input  en10,
  input  en11,
  input  en12,
  input  en13,
  input  SP,
  input  RA,
  input  WriteEnable,
  input  clk,
  output [3:0] R0,
  output [3:0] R1,
  output [3:0] R2,
  output [3:0] R3,
  output [3:0] R4,
  output [3:0] R5,
  output [3:0] R6,
  output [3:0] R7,
  output [3:0] R8,
  output [3:0] R9,
  output [3:0] R10,
  output [3:0] R11,
  output [3:0] R12,
  output [3:0] R13,
  output [3:0] SP_2,
  output [3:0] RA_2
);

  wire and_1_out, and_2_out, and_3_out, and_4_out, and_5_out, and_6_out, and_7_out, and_8_out, and_9_out,
       and_10_out, and_11_out, and_12_out, and_13_out, and_14_out, and_15_out, and_16_out;

  and and_1 (and_1_out, en0, WriteEnable);
  and and_2 (and_2_out, en1, WriteEnable);
  and and_3 (and_3_out, en2, WriteEnable);
  and and_4 (and_4_out, en3, WriteEnable);
  and and_5 (and_5_out, en4, WriteEnable);
  and and_6 (and_6_out, en5, WriteEnable);
  and and_7 (and_7_out, en6, WriteEnable);
  and and_8 (and_8_out, en7, WriteEnable);
  and and_9 (and_9_out, en8, WriteEnable);
  and and_10 (and_10_out, en9, WriteEnable);
  and and_11 (and_11_out, en10, WriteEnable);
  and and_12 (and_12_out, en11, WriteEnable);
  and and_13 (and_13_out, en12, WriteEnable);
  and and_14 (and_14_out, en13, WriteEnable);
  and and_15 (and_15_out, SP, WriteEnable);
  and and_16 (and_16_out, RA, WriteEnable);
  Register #(.width(4)) u_R0 (.D(Load), .en(and_1_out), .Q(R0), .clk(clk));  // open: clr
  Register #(.width(4)) u_R1 (.D(Load), .en(and_2_out), .Q(R1), .clk(clk));  // open: clr
  Register #(.width(4)) u_R2 (.D(Load), .en(and_3_out), .Q(R2), .clk(clk));  // open: clr
  Register #(.width(4)) u_R3 (.D(Load), .en(and_4_out), .Q(R3), .clk(clk));  // open: clr
  Register #(.width(4)) u_R4 (.D(Load), .en(and_5_out), .Q(R4), .clk(clk));  // open: clr
  Register #(.width(4)) u_R5 (.D(Load), .en(and_6_out), .Q(R5), .clk(clk));  // open: clr
  Register #(.width(4)) u_R6 (.D(Load), .en(and_7_out), .Q(R6), .clk(clk));  // open: clr
  Register #(.width(4)) u_R7 (.D(Load), .en(and_8_out), .Q(R7), .clk(clk));  // open: clr
  Register #(.width(4)) u_R8 (.D(Load), .en(and_9_out), .Q(R8), .clk(clk));  // open: clr
  Register #(.width(4)) u_R9 (.D(Load), .en(and_10_out), .Q(R9), .clk(clk));  // open: clr
  Register #(.width(4)) u_R10 (.D(Load), .en(and_11_out), .Q(R10), .clk(clk));  // open: clr
  Register #(.width(4)) u_R11 (.D(Load), .en(and_12_out), .Q(R11), .clk(clk));  // open: clr
  Register #(.width(4)) u_R12 (.D(Load), .en(and_13_out), .Q(R12), .clk(clk));  // open: clr
  Register #(.width(4)) u_R13 (.D(Load), .en(and_14_out), .Q(R13), .clk(clk));  // open: clr
  Register #(.width(4)) u_SP (.D(Load), .en(and_15_out), .Q(SP_2), .clk(clk));  // open: clr
  Register #(.width(4)) u_RA (.D(Load), .en(and_16_out), .Q(RA_2), .clk(clk));  // open: clr
endmodule

module ULA (
  input  [3:0] A,
  input  [3:0] B,
  input  C_In,
  input  S2,
  input  S1,
  input  S0,
  output [3:0] SAIDA,
  output C_out,
  output OVERFLOW
);

  wire ula_celula_1bit_1_c_out, ula_celula_1bit_2_c_out, ula_celula_1bit_3_c_out, ula_celula_1bit_4_c_out;
  wire [1:0] not_2_out;

  not not_1 (not_2_out[1], S1);
  not not_2 (not_2_out[0], S0);
  ULA_celula_1bit ula_celula_1bit_1 (
    .A(A[3]), .B(B[3]), .C_in(ula_celula_1bit_2_c_out), .OUT_RESULT(SAIDA[3]), .SEL_OP({S2, not_2_out}),
    .C_out(ula_celula_1bit_1_c_out));
  overflow overflow_1 (
    .A(A[3]), .B(B[3]), .S(SAIDA[3]), .C_IN(ula_celula_1bit_1_c_out), .SELETOR({S2, not_2_out}),
    .OVERFLOW(OVERFLOW));  // open: OVERFLOW_2
  ULA_celula_1bit ula_celula_1bit_2 (
    .A(A[2]), .B(B[2]), .C_in(ula_celula_1bit_3_c_out), .OUT_RESULT(SAIDA[2]), .SEL_OP({S2, not_2_out}),
    .C_out(ula_celula_1bit_2_c_out));
  ULA_celula_1bit ula_celula_1bit_3 (
    .A(A[1]), .B(B[1]), .C_in(ula_celula_1bit_4_c_out), .OUT_RESULT(SAIDA[1]), .SEL_OP({S2, not_2_out}),
    .C_out(ula_celula_1bit_3_c_out));
  ULA_celula_1bit ula_celula_1bit_4 (
    .A(A[0]), .B(B[0]), .C_in(C_In), .OUT_RESULT(SAIDA[0]), .SEL_OP({S2, not_2_out}),
    .C_out(ula_celula_1bit_4_c_out));
  and AND (C_out, ula_celula_1bit_1_c_out, ~S2);  // AND_Gate

  // Notes on the sheet:
  //   S2    S1   S0
  //   0      0      0        CLEAR  
  //   0      0      1          NAND
  //   0      1      0          A  - B
  //   0      1      1          A + B
  //   1      0      0         A xor B 
  //   1      0      1         A or B
  //   1      1      0        A and B
  //   1      1      1       PRESET
  //   Tabela de Operaçoes
  //   OPERAÇAO
endmodule

module ULA_celula_1bit (
  input  A,
  input  B,
  input  C_in,
  input  [2:0] SEL_OP,
  output OUT_RESULT,
  output C_out
);

  wire adder_1_cout, adder_1_out, AND_2_out, AND_out, clear_1_out_3, NAND_out, OR_out, preset_1_out_3,
       subtractor_1_bout, subtractor_1_out, XOR_out;

  clear clear_1 (.in_1(A), .in_2(B), .out_3(clear_1_out_3));
  nand NAND (NAND_out, A, B);
  Adder #(.width(1)) adder_1 (.a(A), .b(B), .out(adder_1_out), .cin(C_in), .cout(adder_1_cout));
  Subtractor #(.width(1)) subtractor_1 (.a(A), .b(B), .out(subtractor_1_out), .bin(C_in), .bout(subtractor_1_bout));
  xor XOR (XOR_out, A, B);
  or OR (OR_out, A, B);
  and AND (AND_out, A, B);
  preset preset_1 (.in_1(A), .in_2(B), .out_3(preset_1_out_3));
  Multiplexer #(.select(3), .enable("false")) multiplexer_1 (
    .in0(clear_1_out_3), .in1(NAND_out), .in2(adder_1_out), .in3(subtractor_1_out), .in4(XOR_out),
    .in5(OR_out), .in6(AND_out), .in7(preset_1_out_3), .out(OUT_RESULT), .sel(SEL_OP));
  and AND_2 (AND_2_out, ~SEL_OP[2], SEL_OP[1], ~SEL_OP[0]);  // AND_Gate
  Multiplexer #(.enable("false")) multiplexer_2 (
    .in0(adder_1_cout), .in1(subtractor_1_bout), .out(C_out), .sel(AND_2_out));
endmodule

module preset (
  input  in_1,
  input  in_2,
  output out_3
);


  assign out_3 = 1'b1;
endmodule

module clear (
  input  in_1,
  input  in_2,
  output out_3
);


  assign out_3 = 1'b0;
endmodule

module overflow (
  input  A,
  input  B,
  input  S,
  input  C_IN,
  input  [2:0] SELETOR,
  output OVERFLOW,
  output OVERFLOW_2
);

  wire AND_3_out, AND_4_out, AND_out, OR_out, undriven;

  and AND (AND_out, SELETOR[0], SELETOR[1], ~undriven);  // AND_Gate
  and AND_2 (AND_out, SELETOR[0], SELETOR[1], ~undriven);  // AND_Gate
  and AND_3 (AND_3_out, ~A, S, ~B);  // AND_Gate
  and AND_4 (AND_4_out, A, ~S, B);  // AND_Gate
  and AND_5 (AND_4_out, A, ~S, B);  // AND_Gate
  or OR (OR_out, AND_3_out, AND_4_out);
  Multiplexer #(.enable("false")) multiplexer_1 (.in0(OR_out), .in1(C_IN), .out(OVERFLOW), .sel(AND_out));
  Multiplexer #(.enable("false")) multiplexer_2 (.in0(OR_out), .in1(C_IN), .out(OVERFLOW), .sel(AND_out));

  assign OVERFLOW_2 = OVERFLOW;
endmodule

module memoria_de_dados (
  input  [3:0] \endereço ,
  input  [7:0] data_in,
  input  Write,
  input  Read,
  input  clock,
  output [7:0] data_out
);

  RAM #(.addrWidth(4), .bus("separate")) ram_1 (
    .addr(\endereço ), .din(data_in), .data(data_out), .str(Write), .clk(clock), .ld(Read));  // open: sel, clr
endmodule

module PC (
  input  [3:0] PC_In,
  input  Seletor_PC,
  input  clk,
  output [3:0] PC
);

  wire [3:0] adder_1_out, multiplexer_1_out;

  Adder #(.width(4)) adder_1 (.a(PC), .b(4'b0001), .out(adder_1_out));  // open: cin, cout
  Multiplexer #(.width(4)) multiplexer_1 (
    .in0(adder_1_out), .in1(PC_In), .out(multiplexer_1_out), .sel(Seletor_PC));  // open: en
  Register #(.width(4)) u_PC (.D(multiplexer_1_out), .Q(PC), .clk(clk));  // open: en, clr

  // Notes on the sheet:
  //   Fazer com que o CC envie 1 ou 2??
endmodule

module ACC (
  input  [3:0] ACC_In,
  input  clk,
  input  ACC_Load,
  output [3:0] ACC_Out
);

  Register #(.width(4)) register_1 (.D(ACC_In), .en(ACC_Load), .Q(ACC_Out), .clk(clk));  // open: clr
endmodule

module CY (
  input  Carry_ULA,
  input  clk,
  input  Carry_Write,
  output Carry_In
);

  Register #(.width(1)) register_1 (.D(Carry_ULA), .en(Carry_Write), .Q(Carry_In), .clk(clk));  // open: clr
endmodule

module Entrada_N (
  input  clk,
  input  N3,
  input  N2,
  input  N1,
  input  N0,
  input  LOAD_IN,
  output [3:0] N
);

  Register #(.width(4)) register_1 (.D({N3, N2, N1, N0}), .en(LOAD_IN), .Q(N), .clk(clk));  // open: clr

  // Notes on the sheet:
  //   Fazer negócio de guardar clique
endmodule

module i_4004 (
  input  N3,
  input  N2,
  input  N1,
  input  N0,
  input  Ligar,
  output out_6,
  output out_7,
  output out_8,
  output out_9
);

  wire clk, CY_carry_in, fib_N, Flag, Timing_and_Control_acc_write, Timing_and_Control_carry_write,
       \Timing_and_Control_fim_instrução , Timing_and_Control_ir_write, Timing_and_Control_memread,
       Timing_and_Control_memwrite, Timing_and_Control_mux_flag_sel, Timing_and_Control_mux_in_de_sel,
       Timing_and_Control_mux_ram_sel, Timing_and_Control_mux_reg_data_sel, Timing_and_Control_reg_write,
       ULA_c_out;
  wire [2:0] Timing_and_Control_alu_op, Timing_and_Control_mux_acc_sel;
  wire [3:0] ACC_Out, Banco_de_Registradores_register_out, bit_extender_1_out, Imediato,
       In_De_crement_reg_new, multiplexer_1_out, multiplexer_3_out, \rom_instruções_1_opcode , ULA_saida;
  wire [7:0] Addr, Data_Mem, multiplexer_2_out, PC, undriven;
  wire [24:0] Ctrl;

  // Probe on Timing_and_Control_mux_acc_sel
  // Probe on ACC_Out
  Bit_Extender #(.out_width(4)) bit_extender_1 (.in(Data_Mem), .out(bit_extender_1_out));
  Multiplexer #(.select(3), .width(4), .enable("false")) multiplexer_1 (
    .in0(ULA_saida), .in1(bit_extender_1_out), .in2(Imediato), .in3(Banco_de_Registradores_register_out),
    .in4({N3, N2, N1, N0}), .out(multiplexer_1_out), .sel(Timing_and_Control_mux_acc_sel));  // open: in5, in6, in7
  ACC ACC (.ACC_In(multiplexer_1_out), .clk(clk), .ACC_Load(Timing_and_Control_acc_write), .ACC_Out(ACC_Out));
  Timing_and_Control Timing_and_Control (
    .Sinais_de_controle(Ctrl), .Adders(Addr), .Ret(Data_Mem), .Flag(Flag), .CLock(clk),
    .Carry_Write(Timing_and_Control_carry_write), .ALU_OP(Timing_and_Control_alu_op),
    .MUX_ACC_Sel(Timing_and_Control_mux_acc_sel), .ACC_Write(Timing_and_Control_acc_write),
    .MUX_In_De_sel(Timing_and_Control_mux_in_de_sel), .MUX_Reg_Data_Sel(Timing_and_Control_mux_reg_data_sel),
    .Reg_Write(Timing_and_Control_reg_write), .MemWrite(Timing_and_Control_memwrite),
    .MemRead(Timing_and_Control_memread), .IR_Write(Timing_and_Control_ir_write),
    .\Fim_Instrução (\Timing_and_Control_fim_instrução ), .MUX_Flag_Sel(Timing_and_Control_mux_flag_sel),
    .MUX_RAM_Sel(Timing_and_Control_mux_ram_sel), .fib_N__Write(fib_N), .PC_Out(PC));  // open: Halt
  Flag_flip_flops flag_flip_flops_1 (
    .Select_Flag(Timing_and_Control_mux_flag_sel), .CLK(clk), .Flag(Flag), .Carry_Test(CY_carry_in),
    .Z_test(ACC_Out));
  ULA ULA (
    .A(ACC_Out), .B(Banco_de_Registradores_register_out), .S2(Timing_and_Control_alu_op[2]),
    .S1(Timing_and_Control_alu_op[1]), .S0(Timing_and_Control_alu_op[0]), .SAIDA(ULA_saida), .C_out(ULA_c_out));  // open: C_In, OVERFLOW
  CY CY (.Carry_ULA(ULA_c_out), .clk(clk), .Carry_Write(Timing_and_Control_carry_write), .Carry_In(CY_carry_in));
  \ROM_Instruções  \rom_instruções_1  (
    .Opcode(\rom_instruções_1_opcode ), .Iniciar(Ligar), .IR_Write(Timing_and_Control_ir_write), .Clk(clk),
    .Adders(Addr), .Imediato(Imediato), .PC_Out(PC));
  Instruction_Decoder_and_Machine_Cycle_Enconding instruction_decoder_and_machine_cycle_enconding_1 (
    .Opcode(\rom_instruções_1_opcode ), .\Fim_instrução (\Timing_and_Control_fim_instrução ),
    .Sinais_de_controle(Ctrl), .Clock(clk));  // open: Reset
  Multiplexer #(.width(8), .enable("false")) multiplexer_2 (
    .in0(undriven), .in1(PC), .out(multiplexer_2_out), .sel(Timing_and_Control_mux_ram_sel));
  memoria_de_dados Mem_de_Dados (
    .\endereço (Banco_de_Registradores_register_out), .data_in(multiplexer_2_out),
    .Write(Timing_and_Control_memwrite), .Read(Timing_and_Control_memread), .clock(clk), .data_out(Data_Mem));
  Bit_Extender #(.out_width(4)) bit_extender_2 (.in(undriven), .out(ACC_Out));
  Multiplexer #(.width(4), .enable("false")) multiplexer_3 (
    .in0(ACC_Out), .in1(In_De_crement_reg_new), .out(multiplexer_3_out),
    .sel(Timing_and_Control_mux_reg_data_sel));
  Banco_de_Registradores Banco_de_Registradores (
    .RD_add(Imediato), .Load_in(multiplexer_3_out), .clk(clk), .RegWrite(Timing_and_Control_reg_write),
    .Read_add(Imediato), .Register_Out(Banco_de_Registradores_register_out));
  In_De_crement In_De_crement (
    .Reg(Banco_de_Registradores_register_out), .Select_SP(Timing_and_Control_mux_in_de_sel),
    .Reg_New(In_De_crement_reg_new));
  Register #(.width(4)) u_fib_N (.D(ACC_Out), .en(fib_N), .Q({out_6, out_7, out_8, out_9}), .clk(clk));  // open: clr

  // Other names for the same wires on the sheet: on = Ligar

  // Notes on the sheet:
  //   imediato
  //   Fazer mux acc reduzido
endmodule

module Banco_de_Registradores (
  input  [3:0] RD_add,
  input  [3:0] Load_in,
  input  clk,
  input  RegWrite,
  input  [3:0] Read_add,
  output [3:0] Register_Out
);

  wire decoder_1_out0, decoder_1_out1, decoder_1_out2, decoder_1_out3, decoder_1_out4, decoder_1_out5,
       decoder_1_out6, decoder_1_out7, decoder_1_out8, decoder_1_out9, decoder_1_out10, decoder_1_out11,
       decoder_1_out12, decoder_1_out13, decoder_1_out14, decoder_1_out15;
  wire [3:0] registradores_1_r0, registradores_1_r1, registradores_1_r2, registradores_1_r3,
       registradores_1_r4, registradores_1_r5, registradores_1_r6, registradores_1_r7, registradores_1_r8,
       registradores_1_r9, registradores_1_r10, registradores_1_r11, registradores_1_r12,
       registradores_1_r13, registradores_1_ra_2, registradores_1_sp_2;

  Decoder #(.select(4)) decoder_1 (
    .out0(decoder_1_out0), .out1(decoder_1_out1), .out2(decoder_1_out2), .out3(decoder_1_out3),
    .out4(decoder_1_out4), .out5(decoder_1_out5), .out6(decoder_1_out6), .out7(decoder_1_out7),
    .out8(decoder_1_out8), .out9(decoder_1_out9), .out10(decoder_1_out10), .out11(decoder_1_out11),
    .out12(decoder_1_out12), .out13(decoder_1_out13), .out14(decoder_1_out14), .out15(decoder_1_out15),
    .sel(RD_add));  // open: en
  registradores registradores_1 (
    .Load(Load_in), .en0(decoder_1_out0), .en1(decoder_1_out1), .en2(decoder_1_out2), .en3(decoder_1_out3),
    .en4(decoder_1_out4), .en5(decoder_1_out5), .en6(decoder_1_out6), .en7(decoder_1_out7),
    .en8(decoder_1_out8), .en9(decoder_1_out9), .en10(decoder_1_out10), .en11(decoder_1_out11),
    .en12(decoder_1_out12), .en13(decoder_1_out13), .SP(decoder_1_out14), .RA(decoder_1_out15),
    .WriteEnable(RegWrite), .clk(clk), .R0(registradores_1_r0), .R1(registradores_1_r1),
    .R2(registradores_1_r2), .R3(registradores_1_r3), .R4(registradores_1_r4), .R5(registradores_1_r5),
    .R6(registradores_1_r6), .R7(registradores_1_r7), .R8(registradores_1_r8), .R9(registradores_1_r9),
    .R10(registradores_1_r10), .R11(registradores_1_r11), .R12(registradores_1_r12),
    .R13(registradores_1_r13), .SP_2(registradores_1_sp_2), .RA_2(registradores_1_ra_2));
  Multiplexer #(.select(4), .width(4)) multiplexer_1 (
    .in0(registradores_1_r0), .in1(registradores_1_r1), .in2(registradores_1_r2), .in3(registradores_1_r3),
    .in4(registradores_1_r4), .in5(registradores_1_r5), .in6(registradores_1_r6), .in7(registradores_1_r7),
    .in8(registradores_1_r8), .in9(registradores_1_r9), .in10(registradores_1_r10),
    .in11(registradores_1_r11), .in12(registradores_1_r12), .in13(registradores_1_r13),
    .in14(registradores_1_sp_2), .in15(registradores_1_ra_2), .out(Register_Out), .sel(Read_add));  // open: en
endmodule

module Timing_and_Control (
  input  [24:0] Sinais_de_controle,
  input  [7:0] Adders,
  input  [7:0] Ret,
  input  Flag,
  output CLock,
  output Carry_Write,
  output [2:0] ALU_OP,
  output [2:0] MUX_ACC_Sel,
  output ACC_Write,
  output MUX_In_De_sel,
  output MUX_Reg_Data_Sel,
  output Reg_Write,
  output MemWrite,
  output MemRead,
  output IR_Write,
  output \Fim_Instrução ,
  output MUX_Flag_Sel,
  output MUX_RAM_Sel,
  output fib_N__Write,
  output Halt,
  output [7:0] PC_Out
);

  Clock clock_1 (.out(CLock));
  // Probe on Sinais_de_controle[17:16]
  PC_Circuit PC_Circuit (
    .Addr(Adders), .Ret(Ret), .Seletor_PC(Sinais_de_controle[17:16]), .PC_Write(Sinais_de_controle[18]),
    .Branch(Sinais_de_controle[20]), .Flag(Flag), .clk(CLock), .PC(PC_Out));

  assign ACC_Write = Sinais_de_controle[7];
  assign ALU_OP = Sinais_de_controle[3:1];
  assign Carry_Write = Sinais_de_controle[0];
  assign fib_N__Write = Sinais_de_controle[23];
  assign \Fim_Instrução  = Sinais_de_controle[19];
  assign Halt = Sinais_de_controle[24];
  assign IR_Write = Sinais_de_controle[15];
  assign MemRead = Sinais_de_controle[14];
  assign MemWrite = Sinais_de_controle[13];
  assign MUX_ACC_Sel = Sinais_de_controle[6:4];
  assign MUX_Flag_Sel = Sinais_de_controle[21];
  assign MUX_In_De_sel = Sinais_de_controle[8];
  assign MUX_RAM_Sel = Sinais_de_controle[22];
  assign MUX_Reg_Data_Sel = Sinais_de_controle[9];
  assign Reg_Write = Sinais_de_controle[10];
  // also tied to GND on the sheet: {Sinais_de_controle[11], Sinais_de_controle[12]}
endmodule

module In_De_crement (
  input  [3:0] Reg,
  input  Select_SP,
  output [3:0] Reg_New
);

  wire [3:0] multiplexer_1_out;

  Multiplexer #(.width(4), .enable("false")) multiplexer_1 (
    .in0(4'b1111), .in1(4'b0001), .out(multiplexer_1_out), .sel(Select_SP));
  Adder #(.width(4)) adder_1 (.a(Reg), .b(multiplexer_1_out), .out(Reg_New));  // open: cin, cout
endmodule

module Flag_flip_flops (
  input  Select_Flag,
  input  CLK,
  input  Carry_Test,
  input  [3:0] Z_test,
  output Flag
);

  wire and_1_out, Carry_test_q, Z_test_qn;

  and and_1 (and_1_out, Z_test[0], Z_test[1], Z_test[2], Z_test[3]);
  D_Flip_Flop u_Z_test (.clk(CLK), .D(and_1_out), .Qn(Z_test_qn));  // open: Q, preset, en, reset
  D_Flip_Flop u_Carry_test (.clk(CLK), .D(Carry_Test), .Q(Carry_test_q));  // open: Qn, preset, en, reset
  Multiplexer #(.enable("false")) multiplexer_1 (.in0(Z_test_qn), .in1(Carry_test_q), .out(Flag), .sel(Select_Flag));
endmodule

module Unidade_Controle (
  input  Clock,
  input  [3:0] Opcode,
  input  Reset,
  output Carry_Write,
  output [2:0] ALU_OP,
  output [2:0] MUX_ACC_Sel,
  output ACC_Write,
  output MUX_In_De_sel,
  output MUX_Reg_Data_Sel,
  output Reg_Write,
  output [1:0] MUX_Addr_Sel,
  output MemWrite,
  output MemRead,
  output IR_Write,
  output [1:0] MUX_Pc_Sel,
  output PC_Write,
  output Branch,
  output MUX_Flag_Sel,
  output MUX_RAM_Sel,
  output fib_N__Write,
  output Halt
);

  wire not_1_out;
  wire [2:0] counter_1_q;
  wire [19:0] rom_1_data;

  Counter #(.width(3), .max('h7)) counter_1 (
    .load(rom_1_data[19]), .D(3'b000), .count(not_1_out), .Q(counter_1_q), .clk(Clock), .clr(Reset));  // open: carry
  not not_1 (not_1_out, rom_1_data[19]);
  ROM #(.addrWidth(7), .dataWidth(25)) rom_1 (
    .addr({Opcode, counter_1_q}),
    .data({Halt, fib_N__Write, MUX_RAM_Sel, MUX_Flag_Sel, Branch, rom_1_data[19], PC_Write, MUX_Pc_Sel, IR_Write, MemRead, MemWrite, MUX_Addr_Sel, Reg_Write, MUX_Reg_Data_Sel, MUX_In_De_sel, ACC_Write, MUX_ACC_Sel, ALU_OP, rom_1_data[0]}));  // open: sel

  // Notes on the sheet:
  //   contents of rom_1 (hex, n*v repeats v):
  //   4c000 800c0 6*0 4c000 800a0 6*0 4c000 800b0 6*0 4c000 80400 6*0 4c000 80081 6*0 4c000 80083 6*0
  //   4c000 400 83000 5*0 4c000 5090 500 80400 4*0 4c000 400 403000 d0000 4*0 4c000 5000 500 e0000 4*0
  //   4c000 44000 d0000 5*0 4c000 44000 1d0000 5*0 4c000 44000 3c0000 5*0 4c000 82800 6*0 4c000 1000000
  //   6*0 4c000 880000
endmodule

module Instruction_Decoder_and_Machine_Cycle_Enconding (
  input  \Fim_instrução ,
  input  [3:0] Opcode,
  input  Clock,
  input  Reset,
  output [24:0] Sinais_de_controle
);

  wire not_1_out;
  wire [2:0] counter_1_q;

  not not_1 (not_1_out, \Fim_instrução );
  Counter #(.width(3), .max('h7)) counter_1 (
    .load(\Fim_instrução ), .D(3'b000), .count(not_1_out), .Q(counter_1_q), .clk(Clock), .clr(Reset));  // open: carry
  ROM #(.addrWidth(7), .dataWidth(25)) rom_1 (.addr({Opcode, counter_1_q}), .data(Sinais_de_controle));  // open: sel

  // Notes on the sheet:
  //   contents of rom_1 (hex, n*v repeats v):
  //   4c000 800c0 6*0 4c000 800a0 6*0 4c000 800b0 6*0 4c000 80400 6*0 4c000 80081 6*0 4c000 80083 6*0
  //   4c000 400 83000 5*0 4c000 5090 500 80400 4*0 4c000 400 403000 d0000 4*0 4c000 5000 500 e0000 4*0
  //   4c000 44000 d0000 5*0 4c000 44000 1d0000 5*0 4c000 44000 3c0000 5*0 4c000 82800 6*0 4c000 1000000
  //   6*0 4c000 880000
endmodule

module PC_Circuit (
  input  [7:0] Addr,
  input  [7:0] Ret,
  input  [1:0] Seletor_PC,
  input  PC_Write,
  input  Branch,
  input  Flag,
  input  clk,
  output [7:0] PC
);

  wire and_1_out, or_1_out;
  wire [7:0] adder_1_out, multiplexer_1_out;

  Adder adder_1 (.a(PC), .b(8'h1), .out(adder_1_out));  // open: cin, cout
  and and_1 (and_1_out, Branch, Flag);
  Multiplexer #(.select(2), .width(8), .enable("false")) multiplexer_1 (
    .in0(adder_1_out), .in2(Addr), .in3(Ret), .out(multiplexer_1_out), .sel(Seletor_PC));  // open: in1
  or or_1 (or_1_out, PC_Write, and_1_out);
  Register u_PC (.D(multiplexer_1_out), .en(or_1_out), .Q(PC), .clk(clk));  // open: clr

  // Notes on the sheet:
  //   PC_SELECT
endmodule

module \ROM_Instruções  (
  input  Iniciar,
  input  [7:0] PC_Out,
  input  IR_Write,
  input  Clk,
  output [3:0] Opcode,
  output [7:0] Adders,
  output [3:0] Imediato
);

  wire [7:0] rom_1_data;

  ROM rom_1 (.addr(PC_Out), .data(rom_1_data), .sel(Iniciar));
  Instruction_Register Instruction_Register (
    .Opcode(Opcode), .Instruction(rom_1_data), .IR_Write(IR_Write), .clk(Clk), .Addr(Adders),
    .Imediato(Imediato));

  // Notes on the sheet:
  //   contents of rom_1 (hex, n*v repeats v):
  //   0 b0 2c 8e 8 f0 a0 0 32 2f 6e 22 6e 12 31 22 51 c0 26 11 34 22 54 8e 8 33 7e 32 12 34 22 54 8e 8 43
  //   7e 3f 9e 11 7e 32 7e 3f 9e a0 2c
endmodule

module Instruction_Register (
  input  [7:0] Instruction,
  input  IR_Write,
  input  clk,
  output [7:0] Addr,
  output [3:0] Opcode,
  output [3:0] Imediato
);

  Register register_1 (.D(Instruction), .en(IR_Write), .Q(Addr), .clk(clk));  // open: clr

  assign Imediato = Addr[7:4];
  assign Opcode = Addr[3:0];
endmodule
